// Logisim project 2FD_Group33.circ as structural Verilog: 12 circuits, main circuit main
module main (
  output [11:0] pc,
  output [11:0] r0,
  output [11:0] r1,
  output [11:0] r2,
  output [11:0] r3,
  output [11:0] r4,
  output [11:0] r5,
  output [11:0] r6,
  output [11:0] r7,
  output halt
);

  wire clock, clock_1_out, control_unit_1_alu, memtoreg, memwrite, regdest, reset, write;
  wire [2:0] multiplexer_2_out, rd, rs, rt;
  wire [3:0] ALU_CODE, decoder_1_function_code, decoder_1_op_code;
  wire [11:0] DATA, imm, multiplexer_1_out, n8_bit_register_met_outputs_1_s, n8_bit_register_met_outputs_1_t,
       n12_bit_alu_1_result, ram_2_data;
  wire [15:0] ram_1_data;

  Halt halt_1 (.instruction(ram_1_data), .clock(clock_1_out), .reset(reset), .halt(halt));
  Clock clock_1 (.out(clock_1_out));
  Button u_reset (.out(reset));
  _12_bit_program_counter__PC u_12_bit_program_counter_pc_1 (
    .branch_data({12{1'b0}}), .branch(1'b0), .Jump(1'b0), .reset(reset), .clock(clock), .instruction(pc));
  and and_1 (clock, ~halt, clock_1_out);  // AND_Gate
  RAM #(.addrWidth(12), .dataWidth(16)) ram_1 (
    .addr(pc), .data(ram_1_data), .clk(clock), .ld(1'b1), .clr(reset));  // open: sel
  decoder decoder_1 (
    .curr_instr(ram_1_data), .rs(rs), .rd(rd), .op_code(decoder_1_op_code),
    .function_code(decoder_1_function_code), .rt(rt), .immidiate(imm));
  Control_Unit control_unit_1 (
    ._12_15(decoder_1_op_code), ._0_3(decoder_1_function_code), .ALU_CODE(ALU_CODE), .memToReg(memtoreg),
    .regWrite(write), .regDest(regdest), .ALU(control_unit_1_alu), .memWrite(memwrite));  // open: Jr, J, Jal, imm_unsig, addi_2, ldi, addi
  Multiplexer #(.width(12), .enable("false")) multiplexer_1 (
    .in0(n8_bit_register_met_outputs_1_t), .in1(imm), .out(multiplexer_1_out), .sel(control_unit_1_alu));
  Multiplexer #(.width(3), .disabled(0), .enable("false")) multiplexer_2 (
    .in0(rt), .in1(rd), .out(multiplexer_2_out), .sel(regdest));
  _12_bit_ALU u_12_bit_alu_1 (
    .ALU_code(ALU_CODE), .a(n8_bit_register_met_outputs_1_s), .b(multiplexer_1_out),
    .result(n12_bit_alu_1_result));  // open: overflow
  RAM #(.addrWidth(12), .dataWidth(12), .bus("separate")) ram_2 (
    .addr(n12_bit_alu_1_result), .din(n8_bit_register_met_outputs_1_t), .data(ram_2_data), .str(memwrite),
    .clk(clock), .clr(reset));  // open: sel, ld
  Multiplexer #(.width(12), .enable("false")) multiplexer_3 (
    .in0(n12_bit_alu_1_result), .in1(ram_2_data), .out(DATA), .sel(memtoreg));
  _8_bit_register_met_outputs u_8_bit_register_met_outputs_1 (
    .Data(DATA), .Write(write), .Clock(clock), .Reset(reset), .rt(multiplexer_2_out), .rs(rs), .r0(r0),
    .r1(r1), .r2(r2), .r3(r3), .T(n8_bit_register_met_outputs_1_t), .r4(r4), .r5(r5), .r6(r6), .r7(r7),
    .rd(rd), .S(n8_bit_register_met_outputs_1_s));

  // Notes on the sheet:
  //   current instruction
  //   clock signal
  //   reset button
  //   DO NOT CHANGE THE INPUTS AND OUTPUTS OF THIS CIRCUIT! Do not add/remove inputs or outputs. Do not even change their location or orientation.
endmodule

module Halt (
  input  [15:0] instruction,
  input  clock,
  input  reset,
  output halt
);

  wire and_1_out, comparator_1_eq, comparator_2_gt, counter_1_carry, or_1_out, or_2_out;
  wire [11:0] counter_1_q;

  Comparator #(.width(16), .mode("unsigned")) comparator_1 (
    .a(instruction), .b({16{1'b0}}), .eq(comparator_1_eq));  // open: gt, lt
  Counter #(.width(12), .max('hfff), .trigger("falling")) counter_1 (
    .Q(counter_1_q), .carry(counter_1_carry), .clk(clock), .clr(reset));  // open: load, D, count
  or or_1 (or_1_out, comparator_1_eq, counter_1_carry);
  Comparator #(.width(12), .mode("unsigned")) comparator_2 (
    .a(counter_1_q), .b({12{1'b0}}), .gt(comparator_2_gt));  // open: eq, lt
  or or_2 (or_2_out, halt, and_1_out);
  and and_1 (and_1_out, or_1_out, comparator_2_gt);
  Register #(.width(1)) register_1 (.D(or_2_out), .Q(halt), .clk(clock), .clr(reset));  // open: en

  // Notes on the sheet:
  //   halt becomes and stays asserted if the instruction is 0000 (not in the first clock cycle) or the end of the counter is reached (2^12)
endmodule

module _12_bit_program_counter__PC (
  input  reset,
  input  clock,
  input  [11:0] branch_data,
  input  branch,
  input  Jump,
  output [11:0] instruction
);

  wire xor_1_out;
  wire [11:0] add_1_out_3, add_2_out_3, multiplexer_1_out, multiplexer_2_out;

  ADD add_1 (.in_1(instruction), .in_2(branch_data), .out_3(add_1_out_3));  // open: OVERFLOW
  xor xor_1 (xor_1_out, branch, Jump);
  Multiplexer #(.width(12), .enable("false")) multiplexer_1 (
    .in0(add_1_out_3), .in1(branch_data), .out(multiplexer_1_out), .sel(Jump));
  ADD add_2 (.in_1(instruction), .in_2(12'h1), .out_3(add_2_out_3));  // open: OVERFLOW
  Multiplexer #(.width(12), .enable("false")) multiplexer_2 (
    .in0(add_2_out_3), .in1(multiplexer_1_out), .out(multiplexer_2_out), .sel(xor_1_out));
  _12_bit_register u_12_bit_register_1 (
    .clock(clock), .Write(1'b1), .Reset(reset), .Register(instruction), .Data(multiplexer_2_out));
endmodule

module _8_bit_register_met_outputs (
  input  [11:0] Data,
  input  Write,
  input  [2:0] rd,
  input  Clock,
  input  Reset,
  input  [2:0] rt,
  input  [2:0] rs,
  output [11:0] r0,
  output [11:0] r4,
  output [11:0] r5,
  output [11:0] r1,
  output [11:0] r6,
  output [11:0] T,
  output [11:0] r2,
  output [11:0] r7,
  output [11:0] r3,
  output [11:0] S
);

  wire decoder_1_out1, decoder_1_out2, decoder_1_out3, decoder_1_out4, decoder_1_out5, decoder_1_out6,
       decoder_1_out7;

  Decoder #(.select(3), .disabled(0)) decoder_1 (
    .out1(decoder_1_out1), .out2(decoder_1_out2), .out3(decoder_1_out3), .out4(decoder_1_out4),
    .out5(decoder_1_out5), .out6(decoder_1_out6), .out7(decoder_1_out7), .sel(rd), .en(Write));  // open: out0
  _12_bit_register _12_bit_register (.clock(Clock), .Write(1'b0), .Reset(Reset), .Register(r0), .Data({12{1'b0}}));
  _12_bit_register _12_bit_register_2 (
    .clock(Clock), .Write(decoder_1_out1), .Reset(Reset), .Register(r1), .Data(Data));
  _12_bit_register _12_bit_register_3 (
    .clock(Clock), .Write(decoder_1_out2), .Reset(Reset), .Register(r2), .Data(Data));
  _12_bit_register _12_bit_register_4 (
    .clock(Clock), .Write(decoder_1_out3), .Reset(Reset), .Register(r3), .Data(Data));
  Multiplexer #(.select(3), .width(12), .enable("false")) multiplexer_1 (
    .in0(r0), .in1(r1), .in2(r2), .in3(r3), .in4(r4), .in5(r5), .in6(r6), .in7(r7), .out(T), .sel(rt));
  Multiplexer #(.select(3), .width(12), .enable("false")) multiplexer_2 (
    .in0(r0), .in1(r1), .in2(r2), .in3(r3), .in4(r4), .in5(r5), .in6(r6), .in7(r7), .out(S), .sel(rs));
  _12_bit_register _12_bit_register_5 (
    .clock(Clock), .Write(decoder_1_out4), .Reset(Reset), .Register(r4), .Data(Data));
  _12_bit_register _12_bit_register_6 (
    .clock(Clock), .Write(decoder_1_out5), .Reset(Reset), .Register(r5), .Data(Data));
  _12_bit_register _12_bit_register_7 (
    .clock(Clock), .Write(decoder_1_out6), .Reset(Reset), .Register(r6), .Data(Data));
  _12_bit_register _12_bit_register_8 (
    .clock(Clock), .Write(decoder_1_out7), .Reset(Reset), .Register(r7), .Data(Data));
endmodule

module test (
  output [11:0] pc,
  output [11:0] r0,
  output [11:0] r1,
  output [11:0] r2,
  output [11:0] r3,
  output [11:0] r4,
  output [11:0] r5,
  output [11:0] r6,
  output [11:0] r7,
  output halt
);

  wire clock, clock_1_out, comparator_2_eq, IMM, lw, n12_bit_alu_1_p2, not_1_out, reset, select, sw, unary;
  wire [2:0] multiplexer_3_out;
  wire [3:0] CODE, multiplexer_2_out;
  wire [11:0] bit_extender_1_out, data, multiplexer_5_out, n8_bit_register_met_outputs_1_p9,
       n12_bit_alu_1_p3, ram_2_data;
  wire [15:0] ram_1_data;

  Halt halt_1 (.instruction(ram_1_data), .clock(clock_1_out), .reset(reset), .halt(halt));
  Clock clock_1 (.out(clock_1_out));
  Button u_reset (.out(reset));
  _12_bit_program_counter__PC u_12_bit_program_counter_pc_1 (
    .branch_data({12{1'b0}}), .branch(1'b0), .Jump(1'b0), .reset(reset), .clock(clock), .instruction(pc));
  and and_1 (clock, ~halt, clock_1_out);  // AND_Gate
  Comparator #(.width(4)) comparator_1 (.a(ram_1_data[15:12]), .b(4'b1100), .eq(IMM));  // open: gt, lt
  RAM #(.addrWidth(12), .dataWidth(16)) ram_1 (
    .addr(pc), .data(ram_1_data), .clk(clock), .clr(reset));  // open: sel, ld
  Comparator #(.width(4)) comparator_2 (.a(ram_1_data[15:12]), .b(4'b1100), .eq(comparator_2_eq));  // open: gt, lt
  Multiplexer #(.width(4), .enable("false")) multiplexer_1 (
    .in0(multiplexer_2_out), .in1(4'b0100), .out(CODE), .sel(select));
  Comparator #(.width(4)) comparator_3 (.a(ram_1_data[15:12]), .b(4'b0001), .eq(unary));  // open: gt, lt
  Multiplexer #(.width(4), .enable("false")) multiplexer_2 (
    .in0(ram_1_data[15:12]), .in1(ram_1_data[3:0]), .out(multiplexer_2_out), .sel(unary));
  Comparator #(.width(4)) comparator_4 (.a(ram_1_data[15:12]), .b(4'b1010), .eq(lw));  // open: gt, lt
  or or_1 (select, lw, sw);
  Comparator #(.width(4)) comparator_5 (.a(ram_1_data[15:12]), .b(4'b1011), .eq(sw), .lt(sw));  // open: gt
  Multiplexer #(.width(3), .disabled(0), .enable("false")) multiplexer_3 (
    .in0(ram_1_data[2:0]), .in1(ram_1_data[10:8]), .out(multiplexer_3_out), .sel(select));
  assign bit_extender_1_out = {{8{ram_1_data[3]}}, ram_1_data[3:0]};  // Bit_Extender bit_extender_1
  Multiplexer #(.width(12), .enable("false")) multiplexer_4 (
    .in0(n12_bit_alu_1_p3), .in1(ram_2_data), .out(data), .sel(lw));
  Multiplexer #(.width(12), .disabled(0), .enable("false")) multiplexer_5 (
    .in0(n8_bit_register_met_outputs_1_p9), .in1(bit_extender_1_out), .out(multiplexer_5_out), .sel(select));
  // _12_bit_ALU 12_bit_alu_1: pin names not known; wires that end beside it: multiplexer_5_out, n12_bit_alu_1_p2, n12_bit_alu_1_p3, CODE
  not not_1 (not_1_out, sw);
  // _8_bit_register_met_outputs 8_bit_register_met_outputs_1: pin names not known; wires that end beside it: data, not_1_out, clock, reset, multiplexer_3_out, ram_1_data[6:4], n12_bit_alu_1_p2, ram_1_data[10:8], n8_bit_register_met_outputs_1_p9, r0, r1, r2, r3, r4, r5, r6, r4
  RAM #(.addrWidth(12), .dataWidth(12), .bus("separate")) ram_2 (
    .addr(n12_bit_alu_1_p3), .din(n8_bit_register_met_outputs_1_p9), .data(ram_2_data), .str(sw),
    .clk(clock), .ld(lw), .clr(reset));  // open: sel

  // Notes on the sheet:
  //   current instruction
  //   clock signal
  //   reset button
  //   DO NOT CHANGE THE INPUTS AND OUTPUTS OF THIS CIRCUIT! Do not add/remove inputs or outputs. Do not even change their location or orientation.
  //   neit zeker
endmodule

module data_short (
  input  [11:0] alu,
  input  lw,
  input  [11:0] data_in,
  output [11:0] data_out
);

  wire undriven_2;
  wire [11:0] multiplexer_1_out, undriven;

  Multiplexer #(.width(12), .enable("false")) multiplexer_1 (
    .in0(alu), .in1(data_in), .out(multiplexer_1_out), .sel(lw));
  Multiplexer #(.width(12), .enable("false")) multiplexer_2 (
    .in0(multiplexer_1_out), .in1(undriven), .sel(undriven_2));  // open: out
endmodule

module Control_Unit (
  input  [3:0] _12_15,
  input  [3:0] _0_3,
  output [3:0] ALU_CODE,
  output memToReg,
  output regDest,
  output regWrite,
  output ldi,
  output Jr,
  output memWrite,
  output addi,
  output imm_unsig,
  output J,
  output addi_2,
  output Jal,
  output ALU
);

  wire add, comparator_1_eq;
  wire [3:0] multiplexer_1_out;

  Comparator #(.width(4)) comparator_1 (.a(_12_15), .b(4'b0001), .eq(comparator_1_eq));  // open: gt, lt
  Comparator #(.width(4)) comparator_2 (.a(_12_15), .b(4'b0010), .eq(Jr));  // open: gt, lt
  Comparator #(.width(4)) comparator_3 (.a(_12_15), .b(4'b0011), .eq(J));  // open: gt, lt
  Comparator #(.width(4)) comparator_4 (.a(_12_15), .b(4'b0100), .eq(Jal));  // open: gt, lt
  Multiplexer #(.width(4), .enable("false")) multiplexer_1 (
    .in0(_0_3), .in1(_12_15), .out(multiplexer_1_out), .sel(comparator_1_eq));
  Multiplexer #(.width(4), .enable("false")) multiplexer_2 (
    .in0(multiplexer_1_out), .in1(4'b0100), .out(ALU_CODE), .sel(add));
  Comparator #(.width(4)) comparator_5 (.a(_12_15), .b(4'b1011), .eq(memWrite));  // open: gt, lt
  Comparator #(.width(4)) comparator_6 (.a(_12_15), .b(4'b1100), .eq(imm_unsig));  // open: gt, lt
  Comparator #(.width(4)) comparator_7 (.a(_12_15), .b(4'b1101), .eq(addi_2));  // open: gt, lt
  Comparator #(.width(4)) comparator_8 (.a(_12_15), .b(4'b1010), .eq(memToReg));  // open: gt, lt
  or or_1 (add, memToReg, memWrite);
  or or_2 (ALU, memToReg, memWrite, imm_unsig, addi_2);
  not not_1 (regWrite, memWrite);
  Comparator #(.width(4)) comparator_9 (.a(_12_15), .b(4'b1110), .eq(ldi));  // open: gt, lt
  Comparator #(.width(4)) comparator_10 (.a(_12_15), .b(4'b1101), .eq(addi));  // open: gt, lt

  assign regDest = memWrite;
endmodule

module jr (
  input  [3:0] imm,
  input  [11:0] PC,
  input  JR,
  input  [2:0] rd,
  output [11:0] out
);

  wire [3:0] adder_1_out, bit_extender_1_out;
  wire [11:0] bit_extender_2_out;

  assign bit_extender_1_out = {{1{1'b0}}, rd};  // Bit_Extender bit_extender_1
  Adder #(.width(4)) adder_1 (.a(imm), .b(bit_extender_1_out), .out(adder_1_out));  // open: cin, cout
  assign bit_extender_2_out = {{8{1'b0}}, adder_1_out};  // Bit_Extender bit_extender_2
  Multiplexer #(.width(12), .enable("false")) multiplexer_1 (.in0(PC), .in1(bit_extender_2_out), .out(out), .sel(JR));
  // Probe on out
endmodule

module j (
  input  [11:0] PC,
  input  [7:0] imm,
  input  J,
  output [11:0] out
);

  wire [11:0] bit_extender_1_out;

  assign bit_extender_1_out = {{4{1'b0}}, imm};  // Bit_Extender bit_extender_1
  Multiplexer #(.width(12), .enable("false")) multiplexer_1 (.in0(PC), .in1(bit_extender_1_out), .out(out), .sel(J));
endmodule

module beq (
  input  [2:0] rs,
  input  [2:0] rd,
  output eq
);

  Comparator #(.width(3)) comparator_1 (.a(rs), .b(rd), .eq(eq));  // open: gt, lt
endmodule

module beq_2 (
  input  [11:0] pc,
  input  [3:0] imm,
  input  eq,
  output [11:0] out
);

  wire [11:0] adder_1_out, adder_2_out, bit_extender_1_out;

  assign bit_extender_1_out = {{8{imm[3]}}, imm};  // Bit_Extender bit_extender_1
  Adder #(.width(12)) adder_1 (.a(pc), .b(bit_extender_1_out), .out(adder_1_out));  // open: cin, cout
  Adder #(.width(12)) adder_2 (.a(adder_1_out), .b(12'h1), .out(adder_2_out));  // open: cin, cout
  Multiplexer #(.width(12), .enable("false")) multiplexer_1 (.in0(pc), .in1(adder_2_out), .out(out), .sel(eq));
endmodule

module decoder (
  input  [15:0] curr_instr,
  output [2:0] rs,
  output [2:0] rd,
  output [3:0] op_code,
  output [3:0] function_code,
  output [2:0] rt,
  output [11:0] immidiate
);

  wire comparator_1_eq, comparator_2_eq, comparator_3_eq, not_1_out;
  wire [11:0] bit_extender_1_out, bit_extender_2_out, bit_extender_3_out, multiplexer_1_out;

  assign bit_extender_1_out = {{8{1'b0}}, curr_instr[3:0]};  // Bit_Extender bit_extender_1
  assign bit_extender_2_out = {{4{curr_instr[7]}}, curr_instr[7:0]};  // Bit_Extender bit_extender_2
  Comparator #(.width(4)) comparator_1 (.a(curr_instr[15:12]), .b(4'b1100), .eq(comparator_1_eq));  // open: gt, lt
  Multiplexer #(.width(12), .disabled(0), .enable("false")) multiplexer_1 (
    .in0(bit_extender_1_out), .in1(bit_extender_2_out), .out(multiplexer_1_out), .sel(comparator_1_eq));
  assign bit_extender_3_out = {{8{curr_instr[3]}}, curr_instr[3:0]};  // Bit_Extender bit_extender_3
  Comparator #(.width(4)) comparator_2 (.a(curr_instr[15:12]), .b(4'b1101), .eq(comparator_2_eq));  // open: gt, lt
  Multiplexer #(.width(12), .disabled(0), .enable("false")) multiplexer_2 (
    .in0(multiplexer_1_out), .in1(bit_extender_3_out), .out(immidiate), .sel(comparator_2_eq));
  Comparator #(.width(4)) comparator_3 (.a(curr_instr[15:12]), .b(4'b0001), .eq(comparator_3_eq));  // open: gt, lt
  not not_1 (not_1_out, comparator_3_eq);
  Multiplexer #(.width(4), .disabled(0), .enable("false")) multiplexer_3 (
    .in0(4'b0000), .in1(curr_instr[3:0]), .out(function_code), .sel(not_1_out));
  Multiplexer #(.width(3), .disabled(0), .enable("false")) multiplexer_4 (
    .in0(curr_instr[2:0]), .in1(3'b000), .out(rt), .sel(not_1_out));

  assign op_code = curr_instr[15:12];
  assign rd = curr_instr[10:8];
  assign rs = curr_instr[6:4];
endmodule
